# Fritzing sketch bench (saved by Fritzing 1.0.6)
breadboards: 1

parts:
  Pro_Micro = SparkFun Pro Micro
  Q1_BC547 = NPN-Transistor [part_number=BC547 package="TO92 [THT]"]
  R1_10k = Resistor [resistance=10kΩ package=THT]
  D1_1N4148/1N4007 = Diode [package=diode-1n4148]
  R2_10k = Resistor [resistance=10kΩ package=THT]
  JCOM1 = JCOM1
  JFP1 = JFP1
  ATX_24-pin = ATX 24-pin
  Q2_BC547 = NPN-Transistor [part_number=BC547 package="TO92 [THT]"]
  R3_2_2k = Resistor [resistance=2.2kΩ package=THT]
  R4_10k = Resistor [resistance=10kΩ package=THT]

nets:
  N1: Pro_Micro.GND, Q1_BC547.E, D1_1N4148/1N4007.A, JCOM1.5_GND, Q2_BC547.E, R4_10k.Pin_1
  N2: Pro_Micro.VCC, R2_10k.Pin_1, ATX_24-pin.9_5VSB
  N3: Pro_Micro.D4, R3_2_2k.Pin_0
  N4: Pro_Micro.RXI, Q1_BC547.C, R2_10k.Pin_0
  N5: Q1_BC547.B, R1_10k.Pin_1, D1_1N4148/1N4007.C
  N6: R1_10k.Pin_0, JCOM1.3_SOUT
  N7: JFP1.6_Power_SW, Q2_BC547.C
  N8: Q2_BC547.B, R3_2_2k.Pin_1, R4_10k.Pin_0

notes:
  Этап B (BENCH.md B1–B3), прошивка flash-transistor.
  Q2 C идёт на «горячий» пин PWR SW (≈3,3 V, замер B1).
  Нарисован JFP1 6; если горячий 8 — перекинь провод.
  Второй пин PWR SW не подключать: земля общая
  через JCOM1 5.
  R4 держит Q2 закрытым, пока Pro Micro
  прошивается или перезагружается.

custom parts:
  SparkFun Pro Micro: This tiny little board does all of the neat-o Arduino tricks that you’re familiar with: 4 channels of 10-bit ADC, 5 PWM pins, 12 DIOs as well as hardware serial connections Rx and Tx. Running at 16MHz and 5V, this board will remind you a lot of your other favorite Arduino-compatible boards but this little guy can go just about anywhere. There is a voltage regulator on board so it can accept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
  JCOM1: MSI serial header (NAS)
  JFP1: MSI front panel header (NAS)
  ATX 24-pin: PSU 24-pin plug, mating face
