# Fritzing sketch bench (saved by Fritzing 1.0.6)
breadboards: 1

parts:
  Pro_Micro = SparkFun Pro Micro
  Q1_BC547 = NPN-Transistor [part_number=BC547 package="TO92 [THT]"]
  R1_10k = Resistor [resistance=10kΩ package=THT]
  D1_1N4148/1N4007 = Diode [package=diode-1n4148]
  R2_10k = Resistor [resistance=10kΩ package=THT]
  JCOM1 = JCOM1
  JFP1 = JFP1
  ATX_24-pin = ATX 24-pin
  Relay_board = Waveshare RPi Relay Board
  Case_PWR_SW = Case PWR SW

nets:
  N1: Pro_Micro.GND, Q1_BC547.E, D1_1N4148/1N4007.A, JCOM1.5_GND, Relay_board.6_GND
  N2: Pro_Micro.VCC, R2_10k.Pin_1, ATX_24-pin.9_5VSB, Relay_board.1_3V3, Relay_board.2_5V
  N3: Pro_Micro.D4, Relay_board.37_CH1
  N4: Pro_Micro.RXI, Q1_BC547.C, R2_10k.Pin_0
  N5: Q1_BC547.B, R1_10k.Pin_1, D1_1N4148/1N4007.C
  N6: R1_10k.Pin_0, JCOM1.3_SOUT
  N7: JFP1.6_Power_SW, Relay_board.CH1_COM, Case_PWR_SW.2
  N8: JFP1.8_Power_SW, Relay_board.CH1_NO, Case_PWR_SW.1

notes:
  Этап A (BENCH.md A1–A3), прошивка flash-relay.
  Питание: 5VSB, ATX pin 9 (Dupont сзади штекера).
  USB только для прошивки, не вместе с 5VSB.
  Реле-плата: гнёзда 1 (3V3) и 2 (5V) на «+»,
  6 (GND) на «−», 37 (CH1) на Pro Micro 4.
  Без гнезда 1 оптопара не питается, реле молчит.
  Relay_JMP: перемычка на CH1 (IN_CH1–P25)
  обязательна, без неё 37 ни к чему не подключено.
  Каналы слева направо CH3, CH2, CH1; винты
  клеммника NO, COM, NC (COM посередине).
  Кнопка корпуса — в те же COM и NO, параллельно.
  JFP1/JCOM1: распиновка по мануалу MSI.

custom parts:
  SparkFun Pro Micro: This tiny little board does all of the neat-o Arduino tricks that you’re familiar with: 4 channels of 10-bit ADC, 5 PWM pins, 12 DIOs as well as hardware serial connections Rx and Tx. Running at 16MHz and 5V, this board will remind you a lot of your other favorite Arduino-compatible boards but this little guy can go just about anywhere. There is a voltage regulator on board so it can accept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
  JCOM1: MSI serial header (NAS)
  JFP1: MSI front panel header (NAS)
  ATX 24-pin: PSU 24-pin plug, mating face
  Waveshare RPi Relay Board: 3-channel relay HAT. CH1/CH2/CH3 = header pins 37/38/40 (BCM 26/20/21), active LOW, only through the Relay_JMP jumpers. Powered from header pins 2 (5V), 1 (3V3, optocoupler side), 6 (GND).
  Case PWR SW: Case power button (front panel lead)
